# Fritzing sketch fridge_door_alt5 (saved by Fritzing 0.9.9b)
breadboards: 1

parts:
  U1 = attiny85 [package=dip]
  Th1 = Temperature Sensor (Thermistor) [thermistor_type=NTC package=THT]
  Th2 = Temperature Sensor (Thermistor) [thermistor_type=NTC package=THT]
  S1_-_Door = Momentary Switch [package=ksa_sealed_tac_switch]
  LED1 = LED - 5mm [color="Red (633nm)" current=0.030 package="5 mm [THT]"]
  S2_-_Reset = Momentary Switch [package=ksa_sealed_tac_switch]
  X1 = USB Connectors [package=usb-mb-h]
  R4_(rst) = Resistor [tolerance=±5% resistance=100k power=0.25 package=THT]
  R5_(pwr) = Resistor [tolerance=±5% resistance=10k power=0.25 package=THT]
  R1_(rf) = Resistor [tolerance=±5% resistance=10k power=0.25 package=THT]
  R6_(bzr) = Resistor [tolerance=±5% resistance=220 power=0.25 package=THT]
  R2_(rf) = Resistor [tolerance=±5% resistance=10k power=0.25 package=THT]
  R7_(dv2) = Resistor [tolerance=±5% resistance=1M power=0.25 package=THT]
  C2_-_LPF = Ceramic Capacitor [capacitance=47nF voltage=35V package="200 mil [THT, multilayer]"]
  C1 = Ceramic Capacitor [capacitance="100 nF" voltage=35V package="200 mil [THT, multilayer]"]
  TM1637_Display = TM1637
  L1 = Inductor [inductance=10mH package="1206 [SMD]"]
  R3_(dr) = Resistor [tolerance=±5% resistance=10k power=0.25 package=THT]
  R8_(dv1) = Resistor [tolerance=±5% power=0.25 resistance=500k package=THT]
  R8_(dv1)1 = Resistor [tolerance=±5% power=0.25 resistance=1.5k package=THT]
  C2 = Electrolytic Capacitor [capacitance=100µF voltage=35V package="100 mil [THT, electrolytic]"]
  J1_-_Buzzer = Piezo Speaker

nets:
  N1: U1.Pin_1, S2_-_Reset.4, R4_(rst).Pin_0
  N2: U1.Pin_2, Th2.pin_0, R2_(rf).Pin_0
  N3: U1.Pin_3, Th1.pin_0, R1_(rf).Pin_0
  GND: U1.Pin_4, Th1.pin_1, Th2.pin_1, S1_-_Door.1, S1_-_Door.2, S2_-_Reset.1, S2_-_Reset.2, X1.GND, R5_(pwr).Pin_1, C2_-_LPF.0, C1.0, TM1637_Display.GND, R8_(dv1).Pin_1, C2.-, J1_-_Buzzer.pin1
  N4: U1.Pin_5, R6_(bzr).Pin_1, R3_(dr).Pin_0
  N5: U1.Pin_6, TM1637_Display.DIO
  N6: U1.Pin_7, TM1637_Display.CLK
  N7: U1.Pin_8, LED1.anode, X1.VBUS, R4_(rst).Pin_1, R1_(rf).Pin_1, R2_(rf).Pin_1, R7_(dv2).Pin_0, C1.1, TM1637_Display.VCC, C2.+
  N8: S1_-_Door.4, R3_(dr).Pin_1
  N9: LED1.cathode, R5_(pwr).Pin_0
  N10: X1.D-, R8_(dv1)1.Pin_1
  N11: R6_(bzr).Pin_0, L1.pin_0
  N12: R7_(dv2).Pin_1, R8_(dv1).Pin_0, R8_(dv1)1.Pin_0
  N13: C2_-_LPF.1, L1.pin_1, J1_-_Buzzer.pin2

custom parts:
  TM1637: A 4 7-seg display
